// Logisim project SD_Group15.circ as structural Verilog: 5 circuits, main circuit main
module main (
  output [11:0] pc,
  output [11:0] r0,
  output [11:0] r1,
  output [11:0] r2,
  output [11:0] r3,
  output [11:0] r4,
  output [11:0] r5,
  output [11:0] r6,
  output [11:0] r7,
  output halt
);

  wire ALU_Src, c, clock_1_out, lui, MemRead, MemWrite, RegWrite, reset;
  wire [2:0] decoder_1_rd, decoder_1_rs, decoder_1_rt, opcode;
  wire [3:0] controller_1_alu_operation, decoder_1_function_code;
  wire [11:0] ALU_result, imm, multiplexer_1_out, multiplexer_2_out, multiplexer_3_out, ram_2_data,
       register_file_1_s, register_file_1_t, shifter_1_out;
  wire [15:0] ram_1_data;

  Halt halt_1 (.instruction(ram_1_data), .clock(clock_1_out), .reset(reset), .halt(halt));
  Clock clock_1 (.out(clock_1_out));
  Button u_reset (.out(reset));
  and and_1 (c, ~halt, clock_1_out);  // AND_Gate
  program_counter program_counter_1 (
    .branch_value(pc), .instruction_address(pc), .branch_absolute(1'b0), .branch_relative(1'b0), .C(c),
    .reset(reset));
  RAM #(.addrWidth(12), .dataWidth(16)) ram_1 (
    .addr(pc), .data(ram_1_data), .clk(c), .ld(1'b1), .clr(reset));  // open: sel
  decoder decoder_1 (
    .immediate(imm), .instruction(ram_1_data), .Operation_code(opcode), .rd(decoder_1_rd), .rs(decoder_1_rs),
    .rt(decoder_1_rt), .Function_code(decoder_1_function_code));
  Multiplexer #(.width(12)) multiplexer_1 (
    .in0(imm), .in1(shifter_1_out), .out(multiplexer_1_out), .sel(lui));  // open: en
  Shifter #(.width(12)) shifter_1 (.in(imm), .\dist (4'b0011), .out(shifter_1_out));
  controller controller_1 (
    .operation_code(opcode), .function_code(decoder_1_function_code), .RegWrite(RegWrite), .MemRead(MemRead),
    .ALUSrc(ALU_Src), .MemWrite(MemWrite), .ALU_operation(controller_1_alu_operation), .lui(lui));
  Multiplexer #(.select(3), .width(12)) multiplexer_2 (
    .in0({12{1'b0}}), .in1(ALU_result), .in2(ALU_result), .in3(multiplexer_1_out), .in4(ALU_result),
    .in7(ram_2_data), .out(multiplexer_2_out), .sel(opcode));  // open: in5, in6, en
  register_file register_file_1 (
    .rs(decoder_1_rs), .rt(decoder_1_rt), .rd(decoder_1_rd), .Data(multiplexer_2_out), .write(RegWrite),
    .reset(reset), .C(c), .S(register_file_1_s), .T(register_file_1_t), .r0(r0), .r1(r1), .r2(r2), .r3(r3),
    .n4(r4), .n5(r5), .n6(r6), .n7(r7));
  Multiplexer #(.width(12)) multiplexer_3 (
    .in0(register_file_1_t), .in1(imm), .out(multiplexer_3_out), .sel(ALU_Src));  // open: en
  _12_bit_ALU ALU (
    .ALU_code(controller_1_alu_operation), .a(register_file_1_s), .b(multiplexer_3_out), .result(ALU_result));  // open: Overflow
  RAM #(.addrWidth(12), .dataWidth(12), .bus("separate")) ram_2 (
    .addr(ALU_result), .din(register_file_1_s), .data(ram_2_data), .str(MemWrite), .clk(c), .ld(MemRead),
    .clr(reset));  // open: sel

  // Notes on the sheet:
  //   current instruction
  //   clock signal
  //   reset button
  //   Instructions Ram
  //   DO NOT CHANGE THE INPUTS AND OUTPUTS OF THIS CIRCUIT! Do not add/remove inputs or outputs. Do not even change their location or orientation.
  //   Data Ram
endmodule

module Halt (
  input  [15:0] instruction,
  input  clock,
  input  reset,
  output halt
);

  wire and_1_out, comparator_1_eq, comparator_2_gt, counter_1_carry, or_1_out, or_2_out;
  wire [11:0] counter_1_q;

  Comparator #(.width(16), .mode("unsigned")) comparator_1 (
    .a(instruction), .b({16{1'b0}}), .eq(comparator_1_eq));  // open: gt, lt
  Counter #(.width(12), .max('hfff), .trigger("falling")) counter_1 (
    .Q(counter_1_q), .carry(counter_1_carry), .clk(clock), .clr(reset));  // open: load, D, count
  or or_1 (or_1_out, comparator_1_eq, counter_1_carry);
  Comparator #(.width(12), .mode("unsigned")) comparator_2 (
    .a(counter_1_q), .b({12{1'b0}}), .gt(comparator_2_gt));  // open: eq, lt
  or or_2 (or_2_out, halt, and_1_out);
  and and_1 (and_1_out, or_1_out, comparator_2_gt);
  Register #(.width(1)) register_1 (.D(or_2_out), .Q(halt), .clk(clock), .clr(reset));  // open: en

  // Notes on the sheet:
  //   halt becomes and stays asserted if the instruction is 0000 (not in the first clock cycle) or the end of the counter is reached (2^12)
endmodule

module decoder (
  input  [15:0] instruction,
  output [2:0] Operation_code,
  output [2:0] rd,
  output [2:0] rt,
  output [3:0] Function_code,
  output [2:0] rs,
  output [11:0] immediate
);

  wire and_1_out, ari, loadi, lui_out, or_1_out;
  wire [2:0] immcode;

  and and_1 (and_1_out, immcode[0], instruction[0]);
  Multiplexer #(.width(3)) multiplexer_1 (
    .in0(instruction[9:7]), .in1(instruction[12:10]), .out(rs), .sel(or_1_out));  // open: en
  or or_1 (or_1_out, ari, and_1_out);
  and ldi (immcode[2], loadi, ~instruction[0]);  // AND_Gate
  and lui (lui_out, loadi, instruction[0]);
  or or_2 (immcode[1], lui_out, ari);
  Multiplexer #(.select(3), .width(12)) multiplexer_2 (
    .in0({12{1'b0}}), .in1({{6{1'b0}}, instruction[6:1]}), .in2({3'b000, instruction[9:1]}),
    .in3({12{1'b0}}), .in4({{4{instruction[9]}}, instruction[8:1]}), .in5({12{1'b0}}), .in6({12{1'b0}}),
    .in7({12{1'b0}}), .out(immediate), .sel(immcode));  // open: en
  Comparator #(.width(3)) comparator_1 (.a(instruction[15:13]), .b(3'b111), .eq(immcode[0]));  // open: gt, lt
  Comparator #(.width(3)) comparator_2 (.a(instruction[15:13]), .b(3'b011), .eq(loadi));  // open: gt, lt
  Comparator #(.width(3)) comparator_3 (.a(instruction[15:13]), .b(3'b100), .eq(ari));  // open: gt, lt

  assign Function_code = instruction[3:0];
  assign Operation_code = instruction[15:13];
  assign rd = instruction[12:10];
  assign rt = instruction[6:4];

  // Other names for the same wires on the sheet: lwsw = immcode[0]; ibit = instruction[0];
  //   opcode[2:0] = instruction[15:13]

  // Notes on the sheet:
  //   when instruction is addi, subi or sw, then rs is the same as rd
  //   ldi
  //   lui or arithmetic
  //   lw or sw
  //   100: signed 9 bits
  //   010: unsigned 9 bits
  //   001: unsigned 6 bits
  //   unsigned
  //   immediate extraction
  //   signed
endmodule

module controller (
  input  [2:0] operation_code,
  input  [3:0] function_code,
  output ALUSrc,
  output RegWrite,
  output MemRead,
  output lui,
  output MemWrite,
  output [3:0] ALU_operation
);

  wire comparator_1_eq, comparator_2_eq, comparator_3_eq, comparator_4_eq, comparator_5_eq, comparator_6_eq,
       comparator_7_eq;
  wire [3:0] adder_1_out, multiplexer_1_out;

  Multiplexer #(.width(4)) multiplexer_1 (
    .in0(4'b0000), .in1(4'b0001), .out(multiplexer_1_out), .sel(function_code[0]));  // open: en
  Adder #(.width(4)) adder_1 (.a(function_code), .b(4'b1000), .out(adder_1_out));  // open: cin, cout
  Comparator #(.width(3)) comparator_1 (.a(operation_code), .b(3'b111), .eq(comparator_1_eq));  // open: gt, lt
  Comparator #(.width(3)) comparator_2 (.a(operation_code), .b(3'b111), .eq(comparator_2_eq));  // open: gt, lt
  Multiplexer #(.select(3), .width(4)) multiplexer_2 (
    .in0(function_code), .in1(function_code), .in2(adder_1_out), .in3(4'b1010), .in4(multiplexer_1_out),
    .in7(4'b0000), .out(ALU_operation), .sel(operation_code));  // open: in5, in6, en
  Comparator #(.width(3)) comparator_3 (.a(operation_code), .b(3'b111), .eq(comparator_3_eq));  // open: gt, lt
  nand nand_1 (RegWrite, comparator_1_eq, function_code[0]);
  and and_1 (MemRead, comparator_2_eq, ~function_code[0]);  // AND_Gate
  and and_2 (MemWrite, comparator_3_eq, function_code[0]);
  Comparator #(.width(3)) comparator_4 (.a(operation_code), .b(3'b011), .eq(comparator_4_eq));  // open: gt, lt
  Comparator #(.width(3)) comparator_5 (.a(operation_code), .b(3'b100), .eq(comparator_5_eq));  // open: gt, lt
  Comparator #(.width(3)) comparator_6 (.a(operation_code), .b(3'b111), .eq(comparator_6_eq));  // open: gt, lt
  Comparator #(.width(3)) comparator_7 (.a(operation_code), .b(3'b011), .eq(comparator_7_eq));  // open: gt, lt
  or or_1 (ALUSrc, comparator_4_eq, comparator_5_eq, comparator_6_eq);
  and u_lui (lui, comparator_7_eq, function_code[0]);

  // Other names for the same wires on the sheet: func[3:0] = function_code; immbit = function_code[0];
  //   opcode[2:0] = operation_code

  // Notes on the sheet:
  //   Enable MemRead only for lw
  //   Enable MemWrite only for sw
  //   Enable RegWrite for all instructions except for sw
  //   ALU operation depends on the instruction
  //   Selects the second operand for the ALU, 0 is rt, 1 is immediate
  //   Checking if this is a lui instruction so that I can shift with 3
endmodule

// program\ncounter
module program_counter (
  input  [11:0] branch_value,
  input  branch_absolute,
  input  branch_relative,
  input  C,
  input  reset,
  output [11:0] instruction_address
);

  wire and_1_out, and_2_out;
  wire [11:0] adder_1_out, adder_2_out, multiplexer_1_out, multiplexer_2_out;

  Adder #(.width(12)) adder_1 (.a(instruction_address), .b(branch_value), .out(adder_1_out));  // open: cin, cout
  Multiplexer #(.width(12)) multiplexer_1 (
    .in0(instruction_address), .in1(adder_1_out), .out(multiplexer_1_out), .sel(and_1_out));  // open: en
  and and_1 (and_1_out, branch_relative, ~branch_absolute);  // AND_Gate
  Adder #(.width(12)) adder_2 (.a(multiplexer_1_out), .b(12'h1), .out(adder_2_out));  // open: cin, cout
  and and_2 (and_2_out, branch_absolute, ~branch_relative);  // AND_Gate
  Multiplexer #(.width(12)) multiplexer_2 (
    .in0(adder_2_out), .in1(branch_value), .out(multiplexer_2_out), .sel(and_2_out));  // open: en
  _12_bit_register u_12_bit_register_1 (
    .D(multiplexer_2_out), .reset(reset), .write(1'b1), .out_5(instruction_address), .C(C));
endmodule
