// Logisim project circuit.circ as structural Verilog: 6 circuits, main circuit main
module main (
  input  reset,
  output [7:0] r0,
  output [7:0] r1,
  output [7:0] r3,
  output [7:0] r5,
  output [7:0] r2,
  output [7:0] r4,
  output [7:0] r6,
  output [7:0] r7
);

  wire and_1_out, clock_1_out, comparator_1_eq, comparator_2_eq, comparator_3_eq, comparator_3_gt,
       control_unit_1_branch_absolute, control_unit_1_branch_relative, control_unit_1_memread,
       control_unit_1_memwrite, control_unit_1_regwrite;
  wire [1:0] control_unit_1_alu_op;
  wire [2:0] control_unit_1_msb, control_unit_1_rd, control_unit_1_rs, control_unit_1_rt;
  wire [7:0] alu_1_r, control_unit_1_branch_value, multiplexer_1_out, multiplexer_2_out, multiplexer_3_out,
       multiplexer_4_out, multiplexer_5_out, program_counter_1_instruction_address, ram_2_data,
       register_file_1_ap, register_file_1_s, register_file_1_t;
  wire [8:0] ram_1_data;

  Clock clock_1 (.out(clock_1_out));
  Comparator comparator_1 (.a(ram_2_data), .b({8{1'b0}}), .eq(comparator_1_eq));  // open: gt, lt
  and and_1 (and_1_out, comparator_1_eq, control_unit_1_branch_relative);
  program_counter program_counter_1 (
    .Branch_Offset(control_unit_1_branch_value), .Branch_Relative(and_1_out),
    .Branch_Absolute(control_unit_1_branch_absolute), .C(clock_1_out), .reset(reset),
    .instruction_address(program_counter_1_instruction_address));
  RAM #(.dataWidth(9)) ram_1 (
    .addr(program_counter_1_instruction_address), .data(ram_1_data), .clk(clock_1_out), .clr(reset));  // open: sel, ld
  control_unit control_unit_1 (
    .Instruction(ram_1_data), .rd(control_unit_1_rd), .rs(control_unit_1_rs), .rt(control_unit_1_rt),
    .ALU_op(control_unit_1_alu_op), .regwrite(control_unit_1_regwrite), .memread(control_unit_1_memread),
    .memwrite(control_unit_1_memwrite), .MSB(control_unit_1_msb),
    .branch_relative(control_unit_1_branch_relative), .branch_absolute(control_unit_1_branch_absolute),
    .branch_value(control_unit_1_branch_value));
  Multiplexer #(.width(8)) multiplexer_1 (
    .in0(multiplexer_3_out), .in1(ram_2_data), .out(multiplexer_1_out), .sel(control_unit_1_memread));  // open: en
  register_file register_file_1 (
    .rd(control_unit_1_rd), .C(clock_1_out), .write(control_unit_1_regwrite), .reset(reset),
    .S(register_file_1_s), .T(register_file_1_t), .AP(register_file_1_ap), .Data(multiplexer_1_out),
    .rs(control_unit_1_rs), .rt(control_unit_1_rt), .r0(r0), .r1(r1), .r2(r2), .r3(r3), .r4(r4), .r5(r5),
    .r6(r6), .r7(r7));
  Comparator #(.width(3), .mode("unsigned")) comparator_2 (
    .a(control_unit_1_msb), .b(3'b000), .eq(comparator_2_eq));  // open: gt, lt
  Multiplexer #(.width(8)) multiplexer_2 (
    .in0(register_file_1_t), .in1(8'h1), .out(multiplexer_2_out), .sel(comparator_2_eq));  // open: en
  ALU alu_1 (.Op_code(control_unit_1_alu_op), .A(register_file_1_s), .B(multiplexer_2_out), .R(alu_1_r));
  Multiplexer #(.select(2), .width(8)) multiplexer_3 (
    .in0({8{1'b0}}), .in1(alu_1_r), .in2(alu_1_r), .in3(alu_1_r), .out(multiplexer_3_out),
    .sel(control_unit_1_alu_op));  // open: en
  Comparator #(.width(3), .mode("unsigned")) comparator_3 (
    .a(control_unit_1_msb), .b(3'b011), .gt(comparator_3_gt), .eq(comparator_3_eq));  // open: lt
  Multiplexer #(.width(8)) multiplexer_4 (
    .in0(register_file_1_s), .in1(alu_1_r), .out(multiplexer_4_out), .sel(comparator_3_gt));  // open: en
  Multiplexer #(.width(8)) multiplexer_5 (
    .in0(multiplexer_4_out), .in1(control_unit_1_branch_value), .out(multiplexer_5_out), .sel(comparator_3_eq));  // open: en
  RAM #(.bus("separate")) ram_2 (
    .addr(register_file_1_ap), .din(multiplexer_5_out), .data(ram_2_data), .str(control_unit_1_memwrite),
    .clk(clock_1_out), .ld(control_unit_1_memread), .clr(reset));  // open: sel
endmodule

// PC
module program_counter (
  input  [7:0] Branch_Offset,
  input  Branch_Relative,
  input  Branch_Absolute,
  input  C,
  input  reset,
  output [7:0] instruction_address
);

  wire and_1_out, and_2_out;
  wire [7:0] adder_1_out, adder_2_out, multiplexer_1_out, register_1_q;

  Adder adder_1 (.a(register_1_q), .b(Branch_Offset), .out(adder_1_out));  // open: cin, cout
  Multiplexer #(.width(8)) multiplexer_1 (
    .in0(register_1_q), .in1(adder_1_out), .out(multiplexer_1_out), .sel(and_1_out));  // open: en
  and and_1 (and_1_out, Branch_Relative, ~Branch_Absolute);  // AND_Gate
  Adder adder_2 (.a(multiplexer_1_out), .b(8'h1), .out(adder_2_out));  // open: cin, cout
  Register #(.trigger("falling")) register_1 (.D(adder_2_out), .Q(register_1_q), .clk(C), .clr(reset));  // open: en
  Multiplexer #(.width(8)) multiplexer_2 (
    .in0(register_1_q), .in1(Branch_Offset), .out(instruction_address), .sel(and_2_out));  // open: en
  and and_2 (and_2_out, Branch_Absolute, ~Branch_Relative);  // AND_Gate
endmodule

module ALU (
  input  [1:0] Op_code,
  input  [7:0] A,
  input  [7:0] B,
  output [7:0] R
);

  wire [7:0] adder_1_out, not_1_out, or_1_out, subtractor_1_out;

  assign or_1_out = A | B;  // OR_Gate or_1, 8 bits wide
  Adder adder_1 (.a(A), .b(B), .out(adder_1_out));  // open: cin, cout
  Subtractor subtractor_1 (.a(A), .b(B), .out(subtractor_1_out));  // open: bin, bout
  assign not_1_out = ~A;  // NOT_Gate not_1, 8 bits wide
  Multiplexer #(.select(2), .width(8)) multiplexer_1 (
    .in0(or_1_out), .in1(adder_1_out), .in2(subtractor_1_out), .in3(not_1_out), .out(R), .sel(Op_code));  // open: en
endmodule

// Register File
module register_file (
  input  [2:0] rs,
  input  [2:0] rd,
  input  write,
  input  [7:0] Data,
  input  C,
  input  reset,
  input  [2:0] rt,
  output [7:0] S,
  output [7:0] T,
  output [7:0] AP,
  output [7:0] r0,
  output [7:0] r1,
  output [7:0] r2,
  output [7:0] r3,
  output [7:0] r4,
  output [7:0] r5,
  output [7:0] r6,
  output [7:0] r7
);

  wire and_1_out, and_2_out, and_3_out, and_4_out, and_5_out, and_6_out, and_7_out, decoder_1_out1,
       decoder_1_out2, decoder_1_out3, decoder_1_out4, decoder_1_out5, decoder_1_out6, decoder_1_out7;

  Decoder #(.select(3)) decoder_1 (
    .out1(decoder_1_out1), .out2(decoder_1_out2), .out3(decoder_1_out3), .out4(decoder_1_out4),
    .out5(decoder_1_out5), .out6(decoder_1_out6), .out7(decoder_1_out7), .sel(rd));  // open: out0, en
  and and_1 (and_1_out, decoder_1_out1, write);
  and and_2 (and_2_out, decoder_1_out2, write);
  and and_3 (and_3_out, decoder_1_out3, write);
  and and_4 (and_4_out, decoder_1_out4, write);
  and and_5 (and_5_out, decoder_1_out5, write);
  and and_6 (and_6_out, decoder_1_out6, write);
  and and_7 (and_7_out, decoder_1_out7, write);
  Register #(.trigger("falling")) register_1 (.D({8{1'b0}}), .Q(r0));  // open: en, clk, clr
  Register #(.trigger("falling")) register_2 (.D(Data), .en(and_1_out), .Q(r1), .clk(C), .clr(reset));
  Register #(.trigger("falling")) register_3 (.D(Data), .en(and_2_out), .Q(r2), .clk(C), .clr(reset));
  Register #(.trigger("falling")) register_4 (.D(Data), .en(and_3_out), .Q(r3), .clk(C), .clr(reset));
  Register #(.trigger("falling")) register_5 (.D(Data), .en(and_4_out), .Q(r4), .clk(C), .clr(reset));
  Register #(.trigger("falling")) register_6 (.D(Data), .en(and_5_out), .Q(r5), .clk(C), .clr(reset));
  Register #(.trigger("falling")) register_7 (.D(Data), .en(and_6_out), .Q(r6), .clk(C), .clr(reset));
  Register #(.trigger("falling")) register_8 (.D(Data), .en(and_7_out), .Q(AP), .clk(C), .clr(reset));
  Multiplexer #(.select(3), .width(8)) multiplexer_1 (
    .in0(r0), .in1(r1), .in2(r2), .in3(r3), .in4(r4), .in5(r5), .in6(r6), .in7(AP), .out(S), .sel(rs));  // open: en
  Multiplexer #(.select(3), .width(8)) multiplexer_2 (
    .in0(r0), .in1(r1), .in2(r2), .in3(r3), .in4(r4), .in5(r5), .in6(r6), .in7(AP), .out(T), .sel(rt));  // open: en

  assign r7 = AP;
endmodule

module datapath (
  input  reset,
  output [7:0] r0,
  output [7:0] r1,
  output [7:0] r3,
  output [7:0] r5,
  output [7:0] r2,
  output [7:0] r4,
  output [7:0] r6,
  output [7:0] r7
);

  wire and_1_out, clock_1_out, comparator_1_eq, comparator_2_eq, comparator_3_eq, comparator_3_gt,
       control_unit_1_branch_absolute, control_unit_1_branch_relative, control_unit_1_memread,
       control_unit_1_memwrite, control_unit_1_regwrite;
  wire [1:0] control_unit_1_alu_op;
  wire [2:0] control_unit_1_msb, control_unit_1_rd, control_unit_1_rs, control_unit_1_rt;
  wire [7:0] alu_1_r, control_unit_1_branch_value, multiplexer_1_out, multiplexer_2_out, multiplexer_3_out,
       multiplexer_4_out, multiplexer_5_out, program_counter_1_instruction_address, ram_2_data,
       register_file_1_ap, register_file_1_s, register_file_1_t;
  wire [8:0] ram_1_data;

  Clock clock_1 (.out(clock_1_out));
  Comparator #(.mode("unsigned")) comparator_1 (.a(ram_2_data), .b({8{1'b0}}), .eq(comparator_1_eq));  // open: gt, lt
  and and_1 (and_1_out, ~comparator_1_eq, control_unit_1_branch_relative);  // AND_Gate
  program_counter program_counter_1 (
    .Branch_Offset(control_unit_1_branch_value), .Branch_Relative(and_1_out), .Branch_Absolute(1'b0),
    .C(clock_1_out), .reset(reset), .instruction_address(program_counter_1_instruction_address));
  RAM #(.dataWidth(9)) ram_1 (
    .addr(program_counter_1_instruction_address), .data(ram_1_data), .clk(clock_1_out), .clr(reset));  // open: sel, ld
  control_unit control_unit_1 (
    .Instruction(ram_1_data), .rd(control_unit_1_rd), .rs(control_unit_1_rs), .rt(control_unit_1_rt),
    .ALU_op(control_unit_1_alu_op), .regwrite(control_unit_1_regwrite), .memread(control_unit_1_memread),
    .memwrite(control_unit_1_memwrite), .MSB(control_unit_1_msb),
    .branch_relative(control_unit_1_branch_relative), .branch_absolute(control_unit_1_branch_absolute),
    .branch_value(control_unit_1_branch_value));
  Multiplexer #(.width(8)) multiplexer_1 (
    .in0(multiplexer_3_out), .in1(ram_2_data), .out(multiplexer_1_out), .sel(control_unit_1_memread));  // open: en
  register_file register_file_1 (
    .rd(control_unit_1_rd), .C(clock_1_out), .write(control_unit_1_regwrite), .reset(reset),
    .S(register_file_1_s), .T(register_file_1_t), .AP(register_file_1_ap), .Data(multiplexer_1_out),
    .rs(control_unit_1_rs), .rt(control_unit_1_rt), .r0(r0), .r1(r1), .r2(r2), .r3(r3), .r4(r4), .r5(r5),
    .r6(r6), .r7(r7));
  Comparator #(.width(3), .mode("unsigned")) comparator_2 (
    .a(control_unit_1_msb), .b(3'b000), .eq(comparator_2_eq));  // open: gt, lt
  Multiplexer #(.width(8)) multiplexer_2 (
    .in0(register_file_1_t), .in1(8'h1), .out(multiplexer_2_out), .sel(comparator_2_eq));  // open: en
  ALU alu_1 (.Op_code(control_unit_1_alu_op), .A(register_file_1_s), .B(multiplexer_2_out), .R(alu_1_r));
  Multiplexer #(.select(2), .width(8)) multiplexer_3 (
    .in0({8{1'b0}}), .in1(alu_1_r), .in2(alu_1_r), .in3(alu_1_r), .out(multiplexer_3_out),
    .sel(control_unit_1_alu_op));  // open: en
  Comparator #(.width(3), .mode("unsigned")) comparator_3 (
    .a(control_unit_1_msb), .b(3'b011), .gt(comparator_3_gt), .eq(comparator_3_eq));  // open: lt
  Multiplexer #(.width(8)) multiplexer_4 (
    .in0(register_file_1_s), .in1(alu_1_r), .out(multiplexer_4_out), .sel(comparator_3_gt));  // open: en
  Multiplexer #(.width(8)) multiplexer_5 (
    .in0(multiplexer_4_out), .in1(control_unit_1_branch_value), .out(multiplexer_5_out), .sel(comparator_3_eq));  // open: en
  RAM #(.bus("separate")) ram_2 (
    .addr(register_file_1_ap), .din(multiplexer_5_out), .data(ram_2_data), .str(control_unit_1_memwrite),
    .clk(clock_1_out), .ld(control_unit_1_memread), .clr(reset));  // open: sel
endmodule

// Control Unit
module control_unit (
  input  [8:0] Instruction,
  output [2:0] rd,
  output [2:0] rs,
  output [2:0] rt,
  output [1:0] ALU_op,
  output regwrite,
  output memread,
  output memwrite,
  output [2:0] MSB,
  output branch_relative,
  output branch_absolute,
  output [7:0] branch_value
);

  wire and_2_out, comparator_1_eq, comparator_2_eq, comparator_3_eq, comparator_4_gt, comparator_6_eq,
       comparator_7_eq;

  Comparator #(.width(3), .mode("unsigned")) comparator_1 (
    .a(Instruction[8:6]), .b(3'b000), .eq(comparator_1_eq));  // open: gt, lt
  and and_1 (memread, comparator_1_eq, comparator_2_eq);
  Comparator #(.width(3), .mode("unsigned")) comparator_2 (
    .a(Instruction[2:0]), .b(3'b100), .eq(comparator_2_eq));  // open: gt, lt
  and and_2 (and_2_out, comparator_1_eq, comparator_3_eq);
  Comparator #(.width(3), .mode("unsigned")) comparator_3 (
    .a(Instruction[2:0]), .b(3'b101), .eq(comparator_3_eq));  // open: gt, lt
  Comparator #(.width(3), .mode("unsigned")) comparator_4 (
    .a(Instruction[8:6]), .b(3'b011), .gt(comparator_4_gt));  // open: eq, lt
  Comparator #(.width(3), .mode("unsigned")) comparator_5 (
    .a(Instruction[8:6]), .b(3'b001), .eq(branch_relative));  // open: gt, lt
  Comparator #(.width(3), .mode("unsigned")) comparator_6 (
    .a(Instruction[8:6]), .b(3'b010), .eq(comparator_6_eq));  // open: gt, lt
  Comparator #(.width(3), .mode("unsigned")) comparator_7 (
    .a(Instruction[8:6]), .b(3'b011), .eq(comparator_7_eq));  // open: gt, lt
  and and_3 (regwrite, comparator_1_eq, ~and_2_out);  // AND_Gate
  or or_1 (memwrite, and_2_out, comparator_4_gt);
  or or_2 (branch_absolute, comparator_6_eq, comparator_7_eq);
  Multiplexer #(.select(3), .width(2)) multiplexer_1 (
    .in0(Instruction[1:0]), .in1(Instruction[1:0]), .in2(Instruction[1:0]), .in3(Instruction[1:0]),
    .in4(2'b00), .in5(2'b01), .in6(2'b10), .in7(2'b11), .out(ALU_op), .sel(Instruction[8:6]));  // open: en

  assign branch_value = {2'b00, Instruction[5:0]};
  assign MSB = Instruction[8:6];
  assign rd = Instruction[5:3];
  assign rs = Instruction[5:3];
  assign rt = Instruction[2:0];
endmodule
