// Logisim project CA_Project_2_3-4.circ as structural Verilog: 5 circuits, main circuit 1-Bit Adder
module _1_Bit_Adder (
  input  A,
  input  B,
  input  Cin,
  output S
);

  wire A_prime_B_prime_Ci_out, A_prime_BCi_prime_out, AB_prime_Ci_prime_out, ABCi_out;

  and A_prime_BCi_prime (A_prime_BCi_prime_out, ~A, B, ~Cin);  // AND_Gate
  and A_prime_B_prime_Ci (A_prime_B_prime_Ci_out, ~A, ~B, Cin);  // AND_Gate
  and AB_prime_Ci_prime (AB_prime_Ci_prime_out, A, ~B, ~Cin);  // AND_Gate
  or u_S (S, A_prime_B_prime_Ci_out, A_prime_BCi_prime_out, AB_prime_Ci_prime_out, ABCi_out);
  and ABCi (ABCi_out, A, B, Cin);
endmodule

// 4-bit\nCLA
module _4_Bit_CLA (
  input  Carry_In,
  input  [3:0] A,
  input  [3:0] B,
  output [3:0] S,
  output c3,
  output G,
  output P
);

  wire c1_out, c2_out, g0_out, g1_out, g2_out, g3_out, p0_Ci_out, p0_out, p1___g0_out, p1_out, p1_p0_Ci_out,
       p2___g1_out, p2___p1___g0_out, p2___p1___p0___c0_out, p2_out, p3___g2_out, p3_out, p3_p2_g1_out,
       p3_p2_p1_g0_out;

  or p0 (p0_out, A[0], B[0]);
  and P0_2 (P, p0_out, p1_out, p2_out, p3_out);
  and g0 (g0_out, A[0], B[0]);
  or c1 (c1_out, g0_out, p0_Ci_out);
  or p1 (p1_out, A[1], B[1]);
  and p0_Ci (p0_Ci_out, p0_out, Carry_In);
  and g1 (g1_out, A[1], B[1]);
  and p3___g2 (p3___g2_out, p3_out, g2_out);
  or p2 (p2_out, A[2], B[2]);
  and p3_p2_g1 (p3_p2_g1_out, p3_out, p2_out, g1_out);
  and g2 (g2_out, A[2], B[2]);
  and p3_p2_p1_g0 (p3_p2_p1_g0_out, p3_out, p2_out, p1_out, g0_out);
  and p1___g0 (p1___g0_out, p1_out, g0_out);
  or p3 (p3_out, A[3], B[3]);
  and p1_p0_Ci (p1_p0_Ci_out, p1_out, p0_out, Carry_In);
  or c2 (c2_out, g1_out, p1___g0_out, p1_p0_Ci_out);
  and g3 (g3_out, A[3], B[3]);
  and p2___g1 (p2___g1_out, p2_out, g1_out);
  and p2___p1___g0 (p2___p1___g0_out, p2_out, p1_out, g0_out);
  or u_c3 (c3, g2_out, p2___g1_out, p2___p1___p0___c0_out, p2___p1___g0_out);
  or or_1 (G, g3_out, p3_p2_p1_g0_out, p3_p2_g1_out, p3___g2_out);
  and p2___p1___p0___c0 (p2___p1___p0___c0_out, p2_out, p1_out, p0_out, Carry_In);
  _1_Bit_Adder u_1_bit_adder_1 (.A(A[0]), .B(B[0]), .Cin(Carry_In), .S(S[0]));
  _1_Bit_Adder u_1_bit_adder_2 (.A(A[1]), .B(B[1]), .Cin(c1_out), .S(S[1]));
  _1_Bit_Adder u_1_bit_adder_3 (.A(A[2]), .B(B[2]), .Cin(c2_out), .S(S[2]));
  _1_Bit_Adder u_1_bit_adder_4 (.A(A[3]), .B(B[3]), .Cin(c3), .S(S[3]));
endmodule

module Compare (
  input  C_in,
  input  [11:0] A,
  input  [11:0] B,
  output [11:0] out_4,
  output out_5,
  output [11:0] out_6,
  output out_7
);

  // _12_bit_Two_s_Complement_Ripple_Carry_Adder 12_bit_two_s_complement_ripple_carry_adder_1: pin names not known; wires that end beside it: A, B, C_in, out_4, out_5
  _12_Bit_CLA_new u_12_bit_cla_new_1 (.C0(C_in), .Overflow(out_7), .A(A), .Result(out_6), .B(B));  // open: C4
endmodule

// CLA
module _12_Bit_CLA_new (
  input  C0,
  input  [11:0] A,
  input  [11:0] B,
  output Overflow,
  output C4,
  output [11:0] Result
);

  wire cla_unit_1_c1, cla_unit_1_c2, n4_bit_cla_1_c3, n4_bit_cla_1_g, n4_bit_cla_1_p, n4_bit_cla_2_g,
       n4_bit_cla_2_p, n4_bit_cla_3_g, n4_bit_cla_3_p;

  xor xor_1 (Overflow, C4, n4_bit_cla_1_c3);
  _4_Bit_CLA u_4_bit_cla_1 (
    .Carry_In(cla_unit_1_c2), .A(A[11:8]), .B(B[11:8]), .S(Result[11:8]), .G(n4_bit_cla_1_g),
    .P(n4_bit_cla_1_p), .c3(n4_bit_cla_1_c3));
  _4_Bit_CLA u_4_bit_cla_2 (
    .Carry_In(cla_unit_1_c1), .A(A[7:4]), .B(B[7:4]), .S(Result[7:4]), .G(n4_bit_cla_2_g), .P(n4_bit_cla_2_p));  // open: c3
  CLA_Unit cla_unit_1 (
    .G0(n4_bit_cla_3_g), .P0(n4_bit_cla_3_p), .G1(n4_bit_cla_2_g), .P1(n4_bit_cla_2_p), .G2(n4_bit_cla_1_g),
    .P2(n4_bit_cla_1_p), .C1(cla_unit_1_c1), .C2(cla_unit_1_c2), .C3(C4), .C0(C0));
  _4_Bit_CLA u_4_bit_cla_3 (
    .Carry_In(C0), .A(A[3:0]), .B(B[3:0]), .S(Result[3:0]), .G(n4_bit_cla_3_g), .P(n4_bit_cla_3_p));  // open: c3
endmodule

// Carry-Lookahead Unit
module CLA_Unit (
  input  C0,
  input  G0,
  input  P0,
  input  G1,
  input  P1,
  input  G2,
  input  P2,
  output C1,
  output C2,
  output C3
);

  wire P0___c0_out, P0___P1___c0_out, P0___P1___P2___c0_out, P1___G0_out, P1___P2___G0_out, P2___G1_out;

  and P0___c0 (P0___c0_out, C0, P0);
  and P0___P1___c0 (P0___P1___c0_out, C0, P0, P1);
  and P1___G0 (P1___G0_out, P1, G0);
  and P0___P1___P2___c0 (P0___P1___P2___c0_out, P0, P1, P2, C0);
  and P1___P2___G0 (P1___P2___G0_out, P1, P2, G0);
  and P2___G1 (P2___G1_out, P2, G1);
  or u_C1 (C1, G0, P0___c0_out);
  or or_1 (C2, G1, P0___P1___c0_out, P1___G0_out);
  or or_2 (C3, G2, P0___P1___P2___c0_out, P1___P2___G0_out, P2___G1_out);
endmodule
