// Logisim project CA_Project_3_1.circ as structural Verilog: 5 circuits, main circuit 1-Bit ALU
// 1-Bit\nALU
module _1_Bit_ALU (
  input  A_invert,
  input  B_invert,
  input  Carry_In,
  input  [3:0] OC,
  input  A,
  input  B,
  input  Less,
  output Result,
  output Set,
  output Carry_Out,
  output Overflow
);

  wire AND_out, multiplexer_1_out, multiplexer_2_out, not_1_out, not_2_out, OR_out;

  Multiplexer multiplexer_1 (.in0(A), .in1(not_1_out), .out(multiplexer_1_out), .sel(A_invert));  // open: en
  not not_1 (not_1_out, A);
  Multiplexer multiplexer_2 (.in0(B), .in1(not_2_out), .out(multiplexer_2_out), .sel(B_invert));  // open: en
  not not_2 (not_2_out, B);
  and AND (AND_out, multiplexer_1_out, multiplexer_2_out);
  or OR (OR_out, multiplexer_1_out, multiplexer_2_out);
  _1_Bit_Full_Adder u_1_bit_full_adder_1 (
    .A(multiplexer_1_out), .B(multiplexer_2_out), .Cin(Carry_In), .Sum(Set), .Carry_Out(Carry_Out));
  xor u_Overflow (Overflow, Carry_Out, Carry_In);
  Multiplexer #(.select(4)) multiplexer_3 (
    .in0(AND_out), .in1(OR_out), .in2(Set), .in6(Set), .in7(Less), .out(Result), .sel(OC));  // open: in3, in4, in5, in8, in9, in10, in11, in12, in13, in14, in15, en
endmodule

module _1_Bit_Full_Adder (
  input  A,
  input  B,
  input  Cin,
  output Sum,
  output Carry_Out
);

  wire A_prime_B_prime_Ci_out, A_prime_BCi_prime_out, AB_out, AB_prime_Ci_prime_out, ABCi_out, ACi_out,
       BCi_out;

  and A_prime_B_prime_Ci (A_prime_B_prime_Ci_out, ~A, ~B, Cin);  // AND_Gate
  and A_prime_BCi_prime (A_prime_BCi_prime_out, ~A, B, ~Cin);  // AND_Gate
  or S (Sum, A_prime_B_prime_Ci_out, A_prime_BCi_prime_out, AB_prime_Ci_prime_out, ABCi_out);
  and AB_prime_Ci_prime (AB_prime_Ci_prime_out, A, ~B, ~Cin);  // AND_Gate
  and ABCi (ABCi_out, A, B, Cin);
  and ACi (ACi_out, A, Cin);
  and BCi (BCi_out, B, Cin);
  or Cout (Carry_Out, ACi_out, BCi_out, AB_out);
  and AB (AB_out, A, B);
endmodule

module _12_Bit_ALU (
  input  A_invert,
  input  B_invert,
  input  Carry_In,
  input  [3:0] Operation_Code,
  input  [11:0] A,
  input  [11:0] B,
  output [11:0] out_7
);

  wire _0_carry_out, _1_carry_out, _2_carry_out, _3_carry_out, _4_carry_out, _5_carry_out, _6_carry_out,
       _7_carry_out, _8_carry_out, _9_carry_out, _10_carry_out, _11_set;

  _1_Bit_ALU _0 (
    .A(A[0]), .B(B[0]), .Less(_11_set), .Result(out_7[0]), .A_invert(A_invert), .B_invert(B_invert),
    .Carry_In(Carry_In), .OC(Operation_Code), .Carry_Out(_0_carry_out));  // open: Overflow, Set
  _1_Bit_ALU _1 (
    .A(A[1]), .B(B[1]), .Result(out_7[1]), .A_invert(A_invert), .B_invert(B_invert), .Carry_In(_0_carry_out),
    .OC(Operation_Code), .Carry_Out(_1_carry_out));  // open: Less, Overflow, Set
  _1_Bit_ALU _2 (
    .A(A[2]), .B(B[2]), .Result(out_7[2]), .A_invert(A_invert), .B_invert(B_invert), .Carry_In(_1_carry_out),
    .OC(Operation_Code), .Carry_Out(_2_carry_out));  // open: Less, Overflow, Set
  _1_Bit_ALU _3 (
    .A(A[3]), .B(B[3]), .Result(out_7[3]), .A_invert(A_invert), .B_invert(B_invert), .Carry_In(_2_carry_out),
    .OC(Operation_Code), .Carry_Out(_3_carry_out));  // open: Less, Overflow, Set
  _1_Bit_ALU _4 (
    .A(A[4]), .B(B[4]), .Result(out_7[4]), .A_invert(A_invert), .B_invert(B_invert), .Carry_In(_3_carry_out),
    .OC(Operation_Code), .Carry_Out(_4_carry_out));  // open: Less, Overflow, Set
  _1_Bit_ALU _5 (
    .A(A[5]), .B(B[5]), .Result(out_7[5]), .A_invert(A_invert), .B_invert(B_invert), .Carry_In(_4_carry_out),
    .OC(Operation_Code), .Carry_Out(_5_carry_out));  // open: Less, Overflow, Set
  _1_Bit_ALU _6 (
    .A(A[6]), .B(B[6]), .Result(out_7[6]), .A_invert(A_invert), .B_invert(B_invert), .Carry_In(_5_carry_out),
    .OC(Operation_Code), .Carry_Out(_6_carry_out));  // open: Less, Overflow, Set
  _1_Bit_ALU _7 (
    .A(A[7]), .B(B[7]), .Result(out_7[7]), .A_invert(A_invert), .B_invert(B_invert), .Carry_In(_6_carry_out),
    .OC(Operation_Code), .Carry_Out(_7_carry_out));  // open: Less, Overflow, Set
  _1_Bit_ALU _8 (
    .A(A[8]), .B(B[8]), .Result(out_7[8]), .A_invert(A_invert), .B_invert(B_invert), .Carry_In(_7_carry_out),
    .OC(Operation_Code), .Carry_Out(_8_carry_out));  // open: Less, Overflow, Set
  _1_Bit_ALU _9 (
    .A(A[9]), .B(B[9]), .Result(out_7[9]), .A_invert(A_invert), .B_invert(B_invert), .Carry_In(_8_carry_out),
    .OC(Operation_Code), .Carry_Out(_9_carry_out));  // open: Less, Overflow, Set
  _1_Bit_ALU _10 (
    .A(A[10]), .B(B[10]), .Result(out_7[10]), .A_invert(A_invert), .B_invert(B_invert),
    .Carry_In(_9_carry_out), .OC(Operation_Code), .Carry_Out(_10_carry_out));  // open: Less, Overflow, Set
  _1_Bit_ALU _11 (
    .A(A[11]), .B(B[11]), .Result(out_7[11]), .A_invert(A_invert), .B_invert(B_invert),
    .Carry_In(_10_carry_out), .OC(Operation_Code), .Set(_11_set));  // open: Less, Overflow, Carry_Out
endmodule

module _1_Bit_ALU_new (
  input  Carry_In,
  input  [3:0] OC,
  input  A,
  input  B,
  input  Less_or_Greater,
  output Result,
  output Set,
  output Carry_Out,
  output Overflow
);

  wire ADD_sum, AND_out, not_1_out, not_2_out, not_3_out, OR_out, SUB_carry_out;

  and AND (AND_out, A, B);
  or OR (OR_out, A, B);
  _1_Bit_Full_Adder ADD (.A(A), .B(B), .Cin(Carry_In), .Sum(ADD_sum), .Carry_Out(Carry_Out));
  _1_Bit_Full_Adder SUB (.A(A), .B(not_1_out), .Cin(Carry_In), .Sum(Set), .Carry_Out(SUB_carry_out));
  not not_1 (not_1_out, B);
  xor u_Overflow (Overflow, Carry_Out, Carry_In);
  not not_2 (not_2_out, Less_or_Greater);
  // NOT_Gate not_3 has open pins: in=open, out=not_3_out
  Multiplexer #(.select(4)) multiplexer_1 (
    .in0(ADD_sum), .in1(Set), .in2(AND_out), .in3(OR_out), .in4(Less_or_Greater), .in5(not_2_out),
    .in6(not_3_out), .out(Result), .sel(OC));  // open: in7, in8, in9, in10, in11, in12, in13, in14, in15, en
endmodule

module _12_Bit_ALU_new (
  input  in_1,
  input  [11:0] A,
  input  [11:0] B,
  output [11:0] out_4
);

  wire n12_bit_cla_1_p4, n12_bit_cla_1_p5;

  // _12_Bit_CLA 12_bit_cla_1: pin names not known; wires that end beside it: A, B, in_1, n12_bit_cla_1_p4, n12_bit_cla_1_p5, n12_bit_cla_1_p4, n12_bit_cla_1_p5, out_4
  Multiplexer #(.select(4)) multiplexer_1 ();  // open: in0, in1, in2, in3, in4, in5, in6, in7, in8, in9, in10, in11, in12, in13, in14, in15, out, sel, en
endmodule
